# Fritzing sketch BrewDuino (saved by Fritzing 0.9.2b)
circuit board: 4.80116cm x 4.91363cm
breadboards: 1

parts:
  ATmega328p = atmega328 [package=dip]
  XTAL2 = Crystal [frequency="16 Mhz" package=THT]
  C1 = Ceramic Capacitor [capacitance=22µF package="100 mil [THT, multilayer]"]
  C2 = Ceramic Capacitor [capacitance=22µF package="100 mil [THT, multilayer]"]
  U2 = Voltage Regulator - 5V [package="TO220 [THT]"]
  JP1 = Header 2 [package=screwterminal-3.5mm-2_lock]
  J3 = male pin header, 8 pins [form="♂ (male)"]
  R1 = Resistor [tolerance=±5% resistance=220 package=THT]
  J4 = double row male pin header, 4 pins [form="♂ (male)"]
  C3 = Electrolytic Capacitor [capacitance=100nF package="100 mil [THT, electrolytic]"]
  D1 = Rectifier Diode [part_number=1N4001 package="300 mil [THT]"]
  C4 = Electrolytic Capacitor [capacitance=100nF package="100 mil [THT, electrolytic]"]
  J1 = male pin header, 4 pins [form="♂ (male)"]
  J6 = double row male pin header, 4 pins [form="♂ (male)"]
  J7 = male pin header, 6 pins [form="♂ (male)"]
  J5 = male pin header, 7 pins [form="♂ (male)"]

nets:
  N1: ATmega328p.RESET, J3.pin1
  N2: ATmega328p.D0_(RX), J3.pin2
  N3: ATmega328p.D1_(TX), J3.pin3
  N4: ATmega328p.D2, J3.pin4
  N5: ATmega328p.D3_(PWM), J3.pin5
  N6: ATmega328p.D4, J3.pin6
  5V: ATmega328p.VCC, ATmega328p.AVCC, ATmega328p.AREF, U2.output_voltage, J3.pin7, R1.Pin_1, J4.pin1, J4.pin4, C4.+, J6.pin1, J6.pin4, J7.pin1
  GND: ATmega328p.GND, C1.1, C2.1, U2.GND, J3.pin8, J4.pin2, J4.pin3, C3.-, D1.anode, C4.-, J6.pin2, J6.pin3, J5.pin7
  N7: ATmega328p.XLAT1, XTAL2.pin_1, C1.0
  N8: ATmega328p.XLAT2, XTAL2.pin_0, C2.0
  N9: ATmega328p.D5_(PWM), J1.pin1
  N10: ATmega328p.D6_(PWM), J1.pin2
  N11: ATmega328p.D7, R1.Pin_0, J1.pin3
  N12: ATmega328p.D8, J1.pin4
  N13: ATmega328p.D9_(PWM), J7.pin6
  N14: ATmega328p.D10_(PWM), J7.pin5
  N15: ATmega328p.D11_(PWM), J7.pin4
  N16: ATmega328p.D12, J7.pin3
  N17: ATmega328p.D13, J7.pin2
  N18: ATmega328p.A0, J5.pin6
  N19: ATmega328p.A1, J5.pin5
  N20: ATmega328p.A2, J5.pin4
  N21: ATmega328p.A3, J5.pin3
  N22: ATmega328p.A4, J5.pin2
  N23: ATmega328p.A5, J5.pin1
  N24: U2.input_voltage, JP1.2, C3.+
  N25: JP1.1, D1.cathode

notes:
  VCC
  GND
  D/C
  MOSI
  RST
  SCE
  SCLK
  TMP
  RL1
  BZZ
  BGL
  RL2
  -   +
  BTN
  RT2
  RT1
  TX
  RX
  BrewDuino v1.0
